// Digital circuit MICO XII.dig as structural Verilog
module MICO_XII (
  input  clk
);

  wire [1:0] register_1_q;
  wire [15:0] add_1_s, banco_de_registradores_1_p2, multiplexer_1_out;
  wire [31:0] banco_de_registradores_1_p3, rom_1_d;

  Add add_1 (.a(register_1_q[0]), .b(1'b1), .s(add_1_s[0]));  // open: c_i, c_o
  Multiplexer #(.Bits(16), .Selector_Bits(2)) multiplexer_1 (
    .in_0(add_1_s), .in_2(banco_de_registradores_1_p2), .out(multiplexer_1_out));  // open: sel, in_1, in_3
  Register register_1 (.D(multiplexer_1_out[0]), .C(clk), .en(1'b1), .Q(register_1_q[0]));
  ROM #(.Bits(32)) rom_1 (.A(register_1_q), .D(rom_1_d));  // open: sel
  // Banco_de_registradores banco_de_registradores_1: pin names not known; wires that end beside it: clk, banco_de_registradores_1_p2, banco_de_registradores_1_p3
  Multiplexer #(.Bits(32)) multiplexer_2 (.in_0(banco_de_registradores_1_p3));  // open: sel, in_1, out
  RAMDualPort #(.AddrBits(24), .Bits(32)) ramdualport_1 ();  // open: A, Din, str, C, ld, D
  Seven_Seg seven_seg_1 ();  // open: a, b, c, d, e, f, g, dp
  // Pins of 1 and 2 bits meet at register_1_q
  // Pins of 1 and 16 bits meet at add_1_s
  // Pins of 1 and 16 bits meet at multiplexer_1_out
endmodule
